// Logisim project 4-Bit%20ALU.circ as structural Verilog: 3 circuits, main circuit 4 Bit ALU
module _4_Bit_ALU (
  input  [1:0] cALU,
  input  [3:0] A,
  input  [3:0] B,
  output [3:0] R,
  output Zero,
  output ov_signed,
  output ov_unsigned
);

  wire n1_bit_alu_1_cout, n1_bit_alu_2_cout, n1_bit_alu_3_cout, xor_1_out, xor_2_out, xor_3_out, xor_4_out;

  xor xor_1 (xor_1_out, cALU[1], B[0]);
  xor xor_2 (xor_2_out, cALU[1], B[1]);
  xor xor_3 (xor_3_out, cALU[1], B[2]);
  xor xor_4 (xor_4_out, cALU[1], B[3]);
  _1_Bit_ALU u_1_bit_alu_1 (
    .B(xor_1_out), .A(A[0]), .out_5(R[0]), .Cin(cALU[1]), .OP(cALU[0]), .Cout(n1_bit_alu_1_cout));
  _1_Bit_ALU u_1_bit_alu_2 (
    .B(xor_2_out), .A(A[1]), .out_5(R[1]), .Cin(n1_bit_alu_1_cout), .OP(cALU[0]), .Cout(n1_bit_alu_2_cout));
  _1_Bit_ALU u_1_bit_alu_3 (
    .B(xor_3_out), .A(A[2]), .out_5(R[2]), .Cin(n1_bit_alu_2_cout), .OP(cALU[0]), .Cout(n1_bit_alu_3_cout));
  _1_Bit_ALU u_1_bit_alu_4 (
    .B(xor_4_out), .A(A[3]), .out_5(R[3]), .Cin(n1_bit_alu_3_cout), .OP(cALU[0]), .Cout(ov_unsigned));
  nor nor_1 (Zero, R[0], R[1], R[2], R[3]);
  xor xor_5 (ov_signed, n1_bit_alu_3_cout, ov_unsigned);

  // Notes on the sheet:
  //   Operation   cALU
  //   add          00
  //   and          01
  //   sub          10
endmodule

module _1_Bit_Adder (
  input  A,
  input  B,
  input  Cin,
  output Sum,
  output Cout
);

  wire nand_1_out, nand_2_out, xor_1_out;

  xor xor_1 (xor_1_out, A, B);
  nand nand_1 (nand_1_out, B, A);
  xor xor_2 (Sum, xor_1_out, Cin);
  nand nand_2 (nand_2_out, Cin, xor_1_out);
  nand nand_3 (Cout, nand_2_out, nand_1_out);
endmodule

module _1_Bit_ALU (
  input  Cin,
  input  OP,
  input  A,
  input  B,
  output out_5,
  output Cout
);

  wire and_1_out, n1_bit_adder_1_sum;

  and and_1 (and_1_out, A, B);
  _1_Bit_Adder u_1_bit_adder_1 (.A(A), .B(B), .Cin(Cin), .Sum(n1_bit_adder_1_sum), .Cout(Cout));
  Multiplexer #(.enable("false")) multiplexer_1 (.in0(n1_bit_adder_1_sum), .in1(and_1_out), .out(out_5), .sel(OP));

  // Notes on the sheet:
  //   OPERATION   OP
  //   add             0
  //   and             1
endmodule
