// Logisim project PC%20demo.circ as structural Verilog: 4 circuits, main circuit PC
module Demo_PC (
  input  [7:0] in_1,
  output [7:0] Current_PC,
  output [7:0] Next_PC
);

  wire clock_1_out;

  Adder adder_1 (.A(Current_PC), .B(in_1), .Out(Next_PC));
  PC pc_1 (.IN(Next_PC), .Out(Current_PC), .Clk(clock_1_out));
  Clock clock_1 (.out(clock_1_out));
  LED led_1 (.in(clock_1_out));
endmodule

module PC (
  input  [7:0] IN,
  input  Clk,
  output [7:0] Out
);

  Register PC (.D(IN), .en(1'b1), .Q(Out), .clk(Clk), .clr(1'b0));
endmodule

module _4 (
  output [7:0] _4
);


  assign _4 = 8'h4;
endmodule

module Adder (
  input  [7:0] A,
  input  [7:0] B,
  output [7:0] Out
);

  Adder_part adder_1 (.a(A), .b(B), .out(Out), .cin(1'b0));  // open: cout
endmodule
